// Digital circuit Control Unit.dig as structural Verilog
module Control_Unit (
  input  [3:0] Control,
  input  Clock,
  input  Zero_Flag,
  input  Reset,
  output [1:0] RR1,
  output [1:0] RR2,
  output [1:0] WR,
  output WE,
  output IL,
  output PC__Increment,
  output [3:0] ALU,
  output IF,
  output SLT
);

  wire isa_1_slt, relaydt_1_p4;
  wire [3:0] _4bit_register_1_p4, reset_4_out;

  Reset reset_1 (.out(reset_4_out[0]));
  Reset reset_2 (.out(reset_4_out[1]));
  Reset reset_3 (.out(reset_4_out[2]));
  Reset reset_4 (.out(reset_4_out[3]));
  FED fed_1 (.IN(1'b1), .CLK(1'b1));  // open: OUT
  // RelayDT #(.Bits(4)) relaydt_1: pin names not known; wires that end beside it: reset_4_out, Control, Reset, relaydt_1_p4, 1'b1
  // _4bit_register _4bit_register_1: pin names not known; wires that end beside it: relaydt_1_p4, 1'b1, Clock, _4bit_register_1_p4
  ISA isa_1 (
    .Control(_4bit_register_1_p4), .Opcode(ALU), .RR1(RR1), .RR2(RR2), .WR(WR), .WE(WE), .IL(IL),
    .SLT(isa_1_slt));  // open: ADD, SUB, AND, OR, XOR, NOP
  and and_1 (SLT, isa_1_slt, Zero_Flag);

  assign IF = 1'b0;
  assign PC__Increment = 1'b0;

  // Notes on the sheet:
  //   Clock: Hz: 20
endmodule
