// Digital circuit FED.dig as structural Verilog
module FED (
  input  IN,
  input  CLK,
  output [1:0] OUT
);

  wire and_1_out, and_2_out, and_3_out, and_4_out, not_1_out, not_2_out, not_3_out, not_4_out, or_1_out,
       or_2_out;

  not not_1 (not_1_out, OUT[1]);
  not not_2 (not_2_out, OUT[0]);
  not not_3 (not_3_out, IN);
  not not_4 (not_4_out, IN);
  and and_1 (and_1_out, OUT[1], not_3_out);
  and and_2 (and_2_out, OUT[0], IN);
  and and_3 (and_3_out, not_1_out, not_2_out, IN);
  and and_4 (and_4_out, OUT[0], not_4_out);
  or or_1 (or_1_out, and_1_out, and_2_out);
  or or_2 (or_2_out, and_3_out, and_4_out);
  D_FF D_MSB (.D(or_1_out), .C(CLK), .Q(OUT[1]));  // open: nQ
  D_FF D_LSB (.D(or_2_out), .C(CLK), .Q(OUT[0]));  // open: nQ
endmodule
