// Digital circuit ISA.dig as structural Verilog
module ISA (
  input  [3:0] Control,
  output [3:0] Opcode,
  output [1:0] RR1,
  output [1:0] RR2,
  output [1:0] WR,
  output WE,
  output IL,
  output ADD,
  output SUB,
  output AND,
  output OR,
  output XOR,
  output SLT,
  output NOP
);

  wire _1bit_decoder_1_p6, _1bit_decoder_1_p7, _1bit_decoder_1_p9;

  // _1bit_Decoder _1bit_decoder_1: pin names not known; wires that end beside it: Control[0], Control[1], Control[2], Control[3], NOP, _1bit_decoder_1_p6, _1bit_decoder_1_p7, RR1[0], _1bit_decoder_1_p9, ADD, SUB, AND, OR, XOR, SLT
  or or_1 (IL, _1bit_decoder_1_p6, _1bit_decoder_1_p7);
  or or_2 (WE, SLT, XOR, OR, AND, SUB, ADD, _1bit_decoder_1_p9, RR1[0], _1bit_decoder_1_p7, _1bit_decoder_1_p6);
  or or_3 (WR[0], _1bit_decoder_1_p7, _1bit_decoder_1_p9);
  or or_4 (RR2[0], ADD, SUB, AND, OR, XOR, SLT, 1'b0);

  assign Opcode = {Control[0], Control[1], Control[2], Control[3]};
  assign RR1[1] = 1'b0;
  assign RR2[1] = 1'b0;
  assign WR[1] = 1'b0;
endmodule
