// Digital circuit PC_register.dig as structural Verilog
module PC_register (
  input  [3:0] in,
  input  F,
  input  Clock,
  output [3:0] A
);

  wire [3:0] _4bit_adder_subtractor_1_p4, and_1_out;

  assign and_1_out = 4'b0001 & {4{F}};  // And and_1, 4 bits wide
  // _4bit_Adder_subtractor _4bit_adder_subtractor_1: pin names not known; wires that end beside it: in, and_1_out, 1'b0, _4bit_adder_subtractor_1_p4
  D_FF d_ff_1 (.D(_4bit_adder_subtractor_1_p4[0]), .C(Clock), .Q(A[0]));  // open: nQ
  D_FF d_ff_2 (.D(_4bit_adder_subtractor_1_p4[1]), .C(Clock), .Q(A[1]));  // open: nQ
  D_FF d_ff_3 (.D(_4bit_adder_subtractor_1_p4[2]), .C(Clock), .Q(A[2]));  // open: nQ
  D_FF d_ff_4 (.D(_4bit_adder_subtractor_1_p4[3]), .C(Clock), .Q(A[3]));  // open: nQ
endmodule
